// Logisim project KeyboardDelayClassic.circ as structural Verilog: 1 circuit, main circuit KeyboardDelay
module KeyboardDelay (
  input  [6:0] key_in,
  input  clk,
  input  [15:0] delay,
  output key_clock_enable
);

  wire and_1_out, and_2_out, comparator_2_eq, d_ff_1_q, d_ff_2_q, nor_1_out, not_1_out, or_1_out, s_r_ff_1_q,
       xor_1_out;

  Counter #(.width(16), .max('hffff), .trigger("falling")) counter_1 (
    .load(1'b0), .count(not_1_out), .Q(delay), .clk(clk), .clr(and_1_out));  // open: D, carry
  or or_1 (or_1_out, and_2_out, key_clock_enable);
  // Probe on delay
  not not_1 (not_1_out, s_r_ff_1_q);
  Comparator #(.width(16)) comparator_1 (.a(delay), .b(delay), .eq(key_clock_enable));  // open: gt, lt
  and and_1 (and_1_out, d_ff_1_q, or_1_out);
  D_Flip_Flop #(.trigger("falling")) d_ff_1 (.clk(clk), .D(or_1_out), .Q(d_ff_1_q));  // open: Qn, preset, en, reset
  S_R_Flip_Flop #(.trigger("falling")) s_r_ff_1 (
    .S(key_clock_enable), .clk(clk), .R(and_2_out), .Q(s_r_ff_1_q));  // open: Qn, preset, reset, en
  Comparator #(.width(7)) comparator_2 (.a({7{1'b0}}), .b(key_in), .eq(comparator_2_eq));  // open: gt, lt
  D_Flip_Flop #(.trigger("falling")) d_ff_2 (.clk(clk), .D(nor_1_out), .Q(d_ff_2_q));  // open: Qn, preset, en, reset
  nor nor_1 (nor_1_out, comparator_2_eq, key_clock_enable);
  xor xor_1 (xor_1_out, nor_1_out, d_ff_2_q);
  and and_2 (and_2_out, nor_1_out, xor_1_out);
endmodule
