// Logisim project hackpcEvolutionComponent.circ as structural Verilog: 5 circuits, main circuit KeyboardDelay
module KeyboardDelay (
  input  [6:0] key_in,
  input  clk,
  input  [15:0] delay,
  output key_clock_enable
);

  wire and_1_out, and_2_out, comparator_2_eq, d_ff_1_q, d_ff_2_q, nor_1_out, not_1_out, or_1_out, s_r_ff_1_q,
       xor_1_out;
  wire [15:0] counter_1_q;

  Counter #(.max('hffff), .trigger("falling"), .width(16)) counter_1 (
    .load(1'b0), .count(not_1_out), .Q(counter_1_q), .clk(clk), .clr(and_1_out));  // open: D, carry, up
  and and_1 (and_1_out, or_1_out, d_ff_1_q);
  or or_1 (or_1_out, and_2_out, key_clock_enable);
  Comparator #(.width(16)) comparator_1 (.a(delay), .b(counter_1_q), .eq(key_clock_enable));  // open: gt, lt
  // Probe on counter_1_q
  D_Flip_Flop #(.trigger("falling")) d_ff_1 (.clk(clk), .D(or_1_out), .Q(d_ff_1_q));  // open: Qn, preset, reset
  not not_1 (not_1_out, s_r_ff_1_q);
  S_R_Flip_Flop #(.trigger("falling")) s_r_ff_1 (
    .S(key_clock_enable), .clk(clk), .R(and_2_out), .Q(s_r_ff_1_q));  // open: Qn, preset, reset
  Comparator #(.width(7)) comparator_2 (.a({7{1'b0}}), .b(key_in), .eq(comparator_2_eq));  // open: gt, lt
  nor nor_1 (nor_1_out, comparator_2_eq, key_clock_enable);
  D_Flip_Flop #(.trigger("falling")) d_ff_2 (.clk(clk), .D(nor_1_out), .Q(d_ff_2_q));  // open: Qn, preset, reset
  xor xor_1 (xor_1_out, nor_1_out, d_ff_2_q);
  and and_2 (and_2_out, nor_1_out, xor_1_out);
endmodule

module GraphicCard (
  input  load,
  input  clock,
  input  [15:0] data,
  input  [12:0] address,
  output [3:0] color,
  output l_load,
  output [7:0] l_x,
  output [7:0] l_y,
  output r_load,
  output [7:0] r_x,
  output [7:0] r_y
);

  wire and_1_out, and_2_out, and_3_out, d_ff_1_q, graphicprocesser_1_ready, not_1_out, or_1_out,
       queue_1_available, s_r_ff_1_q;
  wire [28:0] queue_1_data_out, register_1_q;

  not not_1 (not_1_out, load);
  S_R_Flip_Flop #(.trigger("falling")) s_r_ff_1 (
    .S(and_3_out), .R(not_1_out), .clk(clock), .Q(s_r_ff_1_q));  // open: reset, Qn, preset
  and and_1 (and_1_out, and_3_out, ~load);  // AND_Gate
  or or_1 (or_1_out, and_1_out, and_2_out);
  and and_2 (and_2_out, ~load, s_r_ff_1_q);  // AND_Gate
  D_Flip_Flop #(.trigger("falling")) d_ff_1 (.D(or_1_out), .clk(clock), .Q(d_ff_1_q));  // open: Qn, preset, reset
  Queue queue_1 (
    .enqueue(load), .dequeue(or_1_out), .clock(clock), .data({address, data}), .data_out(queue_1_data_out),
    .Available(queue_1_available));
  Register #(.width(29)) register_1 (.D(queue_1_data_out), .en(d_ff_1_q), .clk(clock), .Q(register_1_q));  // open: clr
  and and_3 (and_3_out, queue_1_available, graphicprocesser_1_ready);
  GraphicProcesser graphicprocesser_1 (
    .clock(clock), .data(register_1_q[15:0]), .address(register_1_q[28:16]), .load(d_ff_1_q), .color(color),
    .l_x(l_x), .r_x(r_x), .l_y(l_y), .r_y(r_y), .l_load(l_load), .r_load(r_load),
    .Ready(graphicprocesser_1_ready));
endmodule

module GraphicProcesser (
  input  clock,
  input  [15:0] data,
  input  [12:0] address,
  input  load,
  output [3:0] color,
  output [7:0] l_x,
  output [7:0] r_x,
  output [7:0] l_y,
  output [7:0] r_y,
  output l_load,
  output r_load,
  output Ready
);

  wire and_1_out, comparator_1_eq, comparator_2_gt, d_ff_1_q, d_ff_2_q, multiplexer_2_out, or_1_out,
       or_2_out, or_3_out, s_r_ff_1_q, undriven;
  wire [3:0] counter_1_q;
  wire [7:0] bit_extender_2_out;
  wire [8:0] shifter_1_out;
  wire [16:0] bit_extender_1_out;

  S_R_Flip_Flop #(.trigger("falling")) s_r_ff_1 (
    .S(d_ff_2_q), .R(comparator_1_eq), .clk(clock), .Q(s_r_ff_1_q));  // open: reset, Qn, preset
  D_Flip_Flop #(.trigger("falling")) d_ff_1 (
    .D(comparator_1_eq), .clk(clock), .Q(d_ff_1_q));  // open: Qn, preset, reset
  D_Flip_Flop #(.trigger("falling")) d_ff_2 (.D(load), .clk(clock), .Q(d_ff_2_q));  // open: Qn, preset, reset
  or or_1 (or_1_out, d_ff_1_q, load);
  or or_2 (or_2_out, d_ff_2_q, comparator_2_gt);
  // Shift_Register #(.length(15), .trigger("falling")) shift_register_1: pin names not known; wires that end beside it: d_ff_1_q, d_ff_2_q, s_r_ff_1_q, clock, data[15], data[14], data[13], data[12], data[11], data[10], data[9], data[8], data[7], data[6], data[5], data[4]
  Counter #(.max('hf), .trigger("falling"), .width(4)) counter_1 (
    .clr(or_1_out), .load(1'b0), .up(and_1_out), .count(and_1_out), .clk(clock), .Q(counter_1_q));  // open: D, carry
  and and_1 (and_1_out, or_2_out, ~comparator_1_eq);  // AND_Gate
  assign bit_extender_1_out = {{4{1'b0}}, address};  // Bit_Extender bit_extender_1
  Multiplexer #(.width(4)) multiplexer_1 (.in0(4'b1111), .in1(4'b0000), .out(color), .sel(multiplexer_2_out));
  Multiplexer multiplexer_2 (.in0(undriven), .in1(data[0]), .out(multiplexer_2_out), .sel(d_ff_2_q));
  Shifter #(.width(17)) shifter_1 (.in(bit_extender_1_out), .\dist (5'b00100), .out({l_y, shifter_1_out}));
  or or_3 (or_3_out, comparator_2_gt, d_ff_2_q, load);
  assign bit_extender_2_out = {{4{1'b0}}, counter_1_q};  // Bit_Extender bit_extender_2
  Comparator #(.mode("unsigned"), .width(4)) comparator_1 (
    .a(counter_1_q), .b(4'b1111), .eq(comparator_1_eq));  // open: gt, lt
  Comparator #(.mode("unsigned"), .width(4)) comparator_2 (
    .a(counter_1_q), .b(4'b0000), .gt(comparator_2_gt));  // open: eq, lt
  Adder adder_1 (.a(shifter_1_out[7:0]), .b(bit_extender_2_out), .out(l_x));  // open: cin, cout
  Demultiplexer #(.enable("true")) demultiplexer_1 (
    .out0(l_load), .out1(r_load), .in(1'b1), .sel(shifter_1_out[8]), .en(or_3_out));
  LED led_1 (.in(or_3_out));
  not not_1 (Ready, or_3_out);

  assign r_x = l_x;
  assign r_y = l_y;
endmodule

module Queue (
  input  enqueue,
  input  dequeue,
  input  clock,
  input  [28:0] data,
  output [28:0] data_out,
  output Available
);

  wire and_1_out, and_2_out, and_3_out, cnt_carry, or_1_out;
  wire [12:0] cnt_q, Front_q, multiplexer_1_out, Rear_q;

  and and_1 (and_1_out, enqueue, and_2_out);
  or or_1 (or_1_out, dequeue, enqueue);
  and and_2 (and_2_out, or_1_out, ~cnt_carry);  // AND_Gate
  and and_3 (and_3_out, dequeue, and_2_out);
  Counter #(.max('h1fff), .trigger("falling"), .width(13)) Front (
    .count(and_1_out), .Q(Front_q), .clk(clock));  // open: load, D, carry, up, clr
  Counter #(.max('h1fff), .trigger("falling"), .width(13)) cnt (
    .count(and_2_out), .Q(cnt_q), .carry(cnt_carry), .up(enqueue), .clk(clock));  // open: load, D, clr
  Multiplexer #(.width(13)) multiplexer_1 (.in0(Rear_q), .in1(Front_q), .out(multiplexer_1_out));  // open: sel
  Counter #(.max('h1fff), .trigger("falling"), .width(13)) Rear (
    .count(and_3_out), .Q(Rear_q), .clk(clock));  // open: load, D, carry, up, clr
  RAM #(.addrWidth(13), .dataWidth(29), .trigger("falling")) ram_1 (
    .addr(multiplexer_1_out), .we(enqueue), .oe(1'b1), .clk(clock), .din(data), .dout(data_out));
  Comparator #(.mode("unsigned"), .width(13)) comparator_1 (.a(cnt_q), .b({13{1'b0}}), .gt(Available));  // open: eq, lt
endmodule

module Usage (
);

  wire clock_1_out, clock_2_out, graphiccard_1_r_load, keyboarddelay_1_key_clock_enable, not_1_out,
       rgb_video_1_p1, rgb_video_1_p5;
  wire [3:0] rgb_video_1_p8;
  wire [6:0] keyboard_1_data;
  wire [7:0] graphiccard_1_r_x, graphiccard_1_r_y, rgb_video_1_p6, rgb_video_1_p7;
  wire [12:0] rgb_video_1_p3;
  wire [15:0] rgb_video_1_p2;

  Clock clock_1 (.out(clock_1_out));
  Keyboard #(.buflen(2), .trigger("falling")) keyboard_1 (
    .clk(clock_1_out), .re(keyboarddelay_1_key_clock_enable), .data(keyboard_1_data));  // open: clr, avail
  KeyboardDelay keyboarddelay_1 (
    .delay(16'h25), .key_in(keyboard_1_data), .clk(clock_1_out),
    .key_clock_enable(keyboarddelay_1_key_clock_enable));
  Clock clock_2 (.out(clock_2_out));
  not not_1 (not_1_out, clock_2_out);
  // RGB_Video #(.height(256), .scale(1), .width(256)) rgb_video_1: pin names not known; wires that end beside it: rgb_video_1_p1, rgb_video_1_p2, rgb_video_1_p3, not_1_out, rgb_video_1_p5, rgb_video_1_p6, rgb_video_1_p7, rgb_video_1_p8
  GraphicCard graphiccard_1 (
    .load(rgb_video_1_p1), .clock(clock_2_out), .data(rgb_video_1_p2), .address(rgb_video_1_p3),
    .color(rgb_video_1_p8), .l_load(rgb_video_1_p5), .l_x(rgb_video_1_p6), .l_y(rgb_video_1_p7),
    .r_load(graphiccard_1_r_load), .r_x(graphiccard_1_r_x), .r_y(graphiccard_1_r_y));
  // RGB_Video #(.height(256), .scale(1), .width(256)) rgb_video_2: pin names not known; wires that end beside it: not_1_out, graphiccard_1_r_load, graphiccard_1_r_x, graphiccard_1_r_y, rgb_video_1_p8
endmodule
